// Logisim project ALU.circ as structural Verilog: 28 circuits, main circuit main
// NOT
module main (
  input  A,
  output result
);

  Transistor transistor_1 (.in(1'b1), .out(result), .gate(A));
  Transistor #(.\type ("n")) transistor_2 (.in(1'b0), .out(result), .gate(A));
endmodule

module NOT_GATE (
  input  in_1,
  output out_2
);

  Transistor transistor_1 (.in(1'b1), .out(out_2), .gate(in_1));
  Transistor #(.\type ("n")) transistor_2 (.in(1'b0), .out(out_2), .gate(in_1));
endmodule

module NAND_GATE (
  input  A,
  input  B,
  output result
);

  wire transistor_4_out;

  Transistor transistor_1 (.in(1'b1), .out(result), .gate(A));
  Transistor transistor_2 (.in(1'b1), .out(result), .gate(B));
  Transistor #(.\type ("n")) transistor_3 (.in(transistor_4_out), .out(result), .gate(A));
  Transistor #(.\type ("n")) transistor_4 (.in(1'b0), .out(transistor_4_out), .gate(B));
endmodule

module AND_GATE (
  input  A,
  input  B,
  output result
);

  wire transistor_1_out, transistor_3_out;

  Transistor transistor_1 (.in(1'b1), .out(transistor_1_out), .gate(B));
  Transistor #(.\type ("n")) transistor_2 (.in(transistor_3_out), .out(transistor_1_out), .gate(B));
  Transistor #(.\type ("n")) transistor_3 (.in(1'b0), .out(transistor_3_out), .gate(A));
  Transistor transistor_4 (.in(1'b1), .out(transistor_1_out), .gate(A));
  Transistor transistor_5 (.in(1'b1), .out(result), .gate(transistor_1_out));
  Transistor #(.\type ("n")) transistor_6 (.in(1'b0), .out(result), .gate(transistor_1_out));
endmodule

module NOR_GATE (
  input  A,
  input  B,
  output result
);

  wire transistor_1_out;

  Transistor transistor_1 (.in(1'b1), .out(transistor_1_out), .gate(A));
  Transistor transistor_2 (.in(transistor_1_out), .out(result), .gate(B));
  Transistor #(.\type ("n")) transistor_3 (.in(1'b0), .out(result), .gate(A));
  Transistor #(.\type ("n")) transistor_4 (.in(1'b0), .out(result), .gate(B));
endmodule

module OR_GATE (
  input  A,
  input  B,
  output out_3
);

  wire transistor_1_out, transistor_2_out;

  Transistor #(.\type ("n")) transistor_1 (.in(1'b0), .out(transistor_1_out), .gate(A));
  Transistor transistor_2 (.in(1'b1), .out(transistor_2_out), .gate(A));
  Transistor transistor_3 (.in(transistor_2_out), .out(transistor_1_out), .gate(B));
  Transistor #(.\type ("n")) transistor_4 (.in(1'b0), .out(transistor_1_out), .gate(B));
  Transistor transistor_5 (.in(1'b1), .out(out_3), .gate(transistor_1_out));
  Transistor #(.\type ("n")) transistor_6 (.in(1'b0), .out(out_3), .gate(transistor_1_out));
endmodule

module XOR_GATE (
  input  A,
  input  B,
  output result
);

  wire nand_gate_1_result, nand_gate_2_result, nand_gate_3_result;

  NAND_GATE nand_gate_1 (.A(A), .B(B), .result(nand_gate_1_result));
  NAND_GATE nand_gate_2 (.A(A), .B(nand_gate_1_result), .result(nand_gate_2_result));
  NAND_GATE nand_gate_3 (.A(nand_gate_1_result), .B(B), .result(nand_gate_3_result));
  NAND_GATE nand_gate_4 (.A(nand_gate_2_result), .B(nand_gate_3_result), .result(result));
endmodule

module XNOR_GATE (
  input  A,
  input  B,
  output result
);

  wire xor_gate_1_result;

  XOR_GATE xor_gate_1 (.A(A), .B(B), .result(xor_gate_1_result));
  NOT_GATE not_gate_1 (.in_1(xor_gate_1_result), .out_2(result));
endmodule

module HALF_ADDER (
  input  A,
  input  B,
  output sum,
  output carry
);

  XOR_GATE xor_gate_1 (.A(A), .B(B), .result(sum));
  AND_GATE and_gate_1 (.A(A), .B(B), .result(carry));
endmodule

module ODD (
  input  A,
  input  B,
  input  CARRY_IN,
  output SUM
);

  wire xor_gate_1_result;

  XOR_GATE xor_gate_1 (.A(A), .B(B), .result(xor_gate_1_result));
  XOR_GATE xor_gate_2 (.A(xor_gate_1_result), .B(CARRY_IN), .result(SUM));
endmodule

module MAJ (
  input  A,
  input  B,
  input  CARRY_IN,
  output result
);

  wire and_gate_1_result, and_gate_2_result, xor_gate_1_result;

  AND_GATE and_gate_1 (.A(A), .B(B), .result(and_gate_1_result));
  XOR_GATE xor_gate_1 (.A(A), .B(B), .result(xor_gate_1_result));
  AND_GATE and_gate_2 (.A(xor_gate_1_result), .B(CARRY_IN), .result(and_gate_2_result));
  OR_GATE or_gate_1 (.A(and_gate_1_result), .B(and_gate_2_result), .out_3(result));
endmodule

module Full_adder (
  input  A,
  input  B,
  input  CARRY_IN,
  output SUM,
  output CARRY_OUT
);

  ODD odd_1 (.A(A), .B(B), .CARRY_IN(CARRY_IN), .SUM(SUM));
  MAJ maj_1 (.A(A), .B(B), .CARRY_IN(CARRY_IN), .result(CARRY_OUT));
endmodule

module ADDER_8_BIT (
  input  [7:0] A,
  input  carry,
  input  [7:0] B,
  output [7:0] SUM
);

  wire full_adder_1_carry_out, full_adder_2_carry_out, full_adder_3_carry_out, full_adder_4_carry_out,
       full_adder_5_carry_out, full_adder_6_carry_out, full_adder_7_carry_out;

  // Probe on A
  // Probe on B
  Full_adder full_adder_1 (.A(A[0]), .B(B[0]), .CARRY_IN(carry), .SUM(SUM[0]), .CARRY_OUT(full_adder_1_carry_out));
  Full_adder full_adder_2 (
    .A(A[1]), .B(B[1]), .CARRY_IN(full_adder_1_carry_out), .SUM(SUM[1]), .CARRY_OUT(full_adder_2_carry_out));
  Full_adder full_adder_3 (
    .A(A[2]), .B(B[2]), .CARRY_IN(full_adder_2_carry_out), .SUM(SUM[2]), .CARRY_OUT(full_adder_3_carry_out));
  Full_adder full_adder_4 (
    .A(A[3]), .B(B[3]), .CARRY_IN(full_adder_3_carry_out), .SUM(SUM[3]), .CARRY_OUT(full_adder_4_carry_out));
  Full_adder full_adder_5 (
    .A(A[4]), .B(B[4]), .CARRY_IN(full_adder_4_carry_out), .SUM(SUM[4]), .CARRY_OUT(full_adder_5_carry_out));
  Full_adder full_adder_6 (
    .A(A[5]), .B(B[5]), .CARRY_IN(full_adder_5_carry_out), .SUM(SUM[5]), .CARRY_OUT(full_adder_6_carry_out));
  Full_adder full_adder_7 (
    .A(A[6]), .B(B[6]), .CARRY_IN(full_adder_6_carry_out), .SUM(SUM[6]), .CARRY_OUT(full_adder_7_carry_out));
  Full_adder full_adder_8 (.A(A[7]), .B(B[7]), .CARRY_IN(full_adder_7_carry_out), .SUM(SUM[7]));  // open: CARRY_OUT
  // Probe on SUM
endmodule

module AND_8BIT (
  input  [7:0] A,
  input  [7:0] B,
  output [7:0] result
);

  AND_GATE and_gate_1 (.A(A[0]), .B(B[0]), .result(result[0]));
  AND_GATE and_gate_2 (.A(A[1]), .B(B[1]), .result(result[1]));
  AND_GATE and_gate_3 (.A(A[2]), .B(B[2]), .result(result[2]));
  AND_GATE and_gate_4 (.A(A[3]), .B(B[3]), .result(result[3]));
  AND_GATE and_gate_5 (.A(A[4]), .B(B[4]), .result(result[4]));
  AND_GATE and_gate_6 (.A(A[5]), .B(B[5]), .result(result[5]));
  AND_GATE and_gate_7 (.A(A[6]), .B(B[6]), .result(result[6]));
  AND_GATE and_gate_8 (.A(A[7]), .B(B[7]), .result(result[7]));
endmodule

module XOR_8BIT (
  input  [7:0] A,
  input  [7:0] B,
  output [7:0] result
);

  XOR_GATE xor_gate_1 (.A(A[0]), .B(B[0]), .result(result[0]));
  XOR_GATE xor_gate_2 (.A(A[1]), .B(B[1]), .result(result[1]));
  XOR_GATE xor_gate_3 (.A(A[2]), .B(B[2]), .result(result[2]));
  XOR_GATE xor_gate_4 (.A(A[3]), .B(B[3]), .result(result[3]));
  XOR_GATE xor_gate_5 (.A(A[4]), .B(B[4]), .result(result[4]));
  XOR_GATE xor_gate_6 (.A(A[5]), .B(B[5]), .result(result[5]));
  XOR_GATE xor_gate_7 (.A(A[6]), .B(B[6]), .result(result[6]));
  XOR_GATE xor_gate_8 (.A(A[7]), .B(B[7]), .result(result[7]));
endmodule

module AND_3INPUT (
  input  A,
  input  B,
  input  C,
  output RESULT
);

  wire and_gate_1_result;

  AND_GATE and_gate_1 (.A(A), .B(B), .result(and_gate_1_result));
  AND_GATE and_gate_2 (.A(and_gate_1_result), .B(C), .result(RESULT));
endmodule

module decorder3_8 (
  input  A,
  input  B,
  input  C,
  output s1,
  output s2,
  output s3,
  output s4,
  output s5,
  output s6,
  output s7,
  output s8
);

  wire not_gate_1_out_2, not_gate_2_out_2, not_gate_3_out_2;

  NOT_GATE not_gate_1 (.in_1(A), .out_2(not_gate_1_out_2));
  NOT_GATE not_gate_2 (.in_1(B), .out_2(not_gate_2_out_2));
  NOT_GATE not_gate_3 (.in_1(C), .out_2(not_gate_3_out_2));
  AND_3INPUT and_3input_1 (.A(not_gate_1_out_2), .B(not_gate_2_out_2), .C(not_gate_3_out_2), .RESULT(s1));
  AND_3INPUT and_3input_2 (.A(not_gate_1_out_2), .B(not_gate_2_out_2), .C(C), .RESULT(s2));
  AND_3INPUT and_3input_3 (.A(not_gate_1_out_2), .B(B), .C(not_gate_3_out_2), .RESULT(s3));
  AND_3INPUT and_3input_4 (.A(not_gate_1_out_2), .B(B), .C(C), .RESULT(s4));
  AND_3INPUT and_3input_5 (.A(A), .B(not_gate_2_out_2), .C(not_gate_3_out_2), .RESULT(s5));
  AND_3INPUT and_3input_6 (.A(A), .B(not_gate_2_out_2), .C(C), .RESULT(s6));
  AND_3INPUT and_3input_7 (.A(A), .B(B), .C(not_gate_3_out_2), .RESULT(s7));
  AND_3INPUT and_3input_8 (.A(A), .B(B), .C(C), .RESULT(s8));
endmodule

module demux3_8 (
  input  Singal,
  input  A,
  input  B,
  input  C,
  output s1,
  output s2,
  output s3,
  output s4,
  output s5,
  output s6,
  output s7,
  output s8
);

  wire decorder3_8_1_s1, decorder3_8_1_s2, decorder3_8_1_s3, decorder3_8_1_s4, decorder3_8_1_s5,
       decorder3_8_1_s6, decorder3_8_1_s7, decorder3_8_1_s8;

  decorder3_8 decorder3_8_1 (
    .A(A), .B(B), .C(C), .s1(decorder3_8_1_s1), .s2(decorder3_8_1_s2), .s3(decorder3_8_1_s3),
    .s4(decorder3_8_1_s4), .s5(decorder3_8_1_s5), .s6(decorder3_8_1_s6), .s7(decorder3_8_1_s7),
    .s8(decorder3_8_1_s8));
  AND_GATE and_gate_1 (.A(decorder3_8_1_s1), .B(Singal), .result(s1));
  AND_GATE and_gate_2 (.A(decorder3_8_1_s2), .B(Singal), .result(s2));
  AND_GATE and_gate_3 (.A(decorder3_8_1_s3), .B(Singal), .result(s3));
  AND_GATE and_gate_4 (.A(decorder3_8_1_s4), .B(Singal), .result(s4));
  AND_GATE and_gate_5 (.A(decorder3_8_1_s5), .B(Singal), .result(s5));
  AND_GATE and_gate_6 (.A(decorder3_8_1_s6), .B(Singal), .result(s6));
  AND_GATE and_gate_7 (.A(decorder3_8_1_s7), .B(Singal), .result(s7));
  AND_GATE and_gate_8 (.A(decorder3_8_1_s8), .B(Singal), .result(s8));
endmodule

module decordANDmux (
  input  DATA_IN,
  input  A,
  input  B,
  input  C,
  output S1_1,
  output S1_X,
  output S2_1,
  output S2_X,
  output S3_1,
  output S3_X,
  output S4_1,
  output S4_X,
  output S5_1,
  output S5_X,
  output S6_1,
  output S6_X,
  output S7_1,
  output S7_X,
  output S8_1,
  output S8_X
);

  decorder3_8 decorder3_8_1 (
    .A(A), .B(B), .C(C), .s1(S1_1), .s2(S2_1), .s3(S3_1), .s4(S4_1), .s5(S5_1), .s6(S6_1), .s7(S7_1),
    .s8(S8_1));
  AND_GATE and_gate_1 (.A(S1_1), .B(DATA_IN), .result(S1_X));
  AND_GATE and_gate_2 (.A(S2_1), .B(DATA_IN), .result(S2_X));
  AND_GATE and_gate_3 (.A(S3_1), .B(DATA_IN), .result(S3_X));
  AND_GATE and_gate_4 (.A(S4_1), .B(DATA_IN), .result(S4_X));
  AND_GATE and_gate_5 (.A(S5_1), .B(DATA_IN), .result(S5_X));
  AND_GATE and_gate_6 (.A(S6_1), .B(DATA_IN), .result(S6_X));
  AND_GATE and_gate_7 (.A(S7_1), .B(DATA_IN), .result(S7_X));
  AND_GATE and_gate_8 (.A(S8_1), .B(DATA_IN), .result(S8_X));
endmodule

module OR_8BIT (
  input  [7:0] A,
  input  [7:0] B,
  output [7:0] Result
);

  OR_GATE or_gate_1 (.A(A[0]), .B(B[0]), .out_3(Result[0]));
  OR_GATE or_gate_2 (.A(A[1]), .B(B[1]), .out_3(Result[1]));
  OR_GATE or_gate_3 (.A(A[2]), .B(B[2]), .out_3(Result[2]));
  OR_GATE or_gate_4 (.A(A[3]), .B(B[3]), .out_3(Result[3]));
  OR_GATE or_gate_5 (.A(A[4]), .B(B[4]), .out_3(Result[4]));
  OR_GATE or_gate_6 (.A(A[5]), .B(B[5]), .out_3(Result[5]));
  OR_GATE or_gate_7 (.A(A[6]), .B(B[6]), .out_3(Result[6]));
  OR_GATE or_gate_8 (.A(A[7]), .B(B[7]), .out_3(Result[7]));
endmodule

module OR_3input (
  input  [7:0] A,
  input  [7:0] B,
  input  [7:0] C,
  output [7:0] result
);

  wire [7:0] or_8bit_1_result;

  OR_8BIT or_8bit_1 (.A(A), .B(B), .Result(or_8bit_1_result));
  OR_8BIT or_8bit_2 (.A(or_8bit_1_result), .B(C), .Result(result));
endmodule

module ONE_hot_mux (
  input  add,
  input  sub,
  input  xor_b,
  input  and_b,
  input  r_shift,
  input  l_shift,
  input  sel_add,
  input  sel_sub,
  input  sel_xor,
  input  sel_and,
  input  sel_Rshift,
  input  sel_Lshift,
  output mux_out
);

  wire and_gate_1_result, and_gate_2_result, and_gate_3_result, and_gate_4_result, and_gate_5_result,
       and_gate_6_result;

  AND_GATE and_gate_1 (.A(add), .B(sel_add), .result(and_gate_1_result));
  AND_GATE and_gate_2 (.A(sub), .B(sel_sub), .result(and_gate_2_result));
  AND_GATE and_gate_3 (.A(xor_b), .B(sel_xor), .result(and_gate_3_result));
  AND_GATE and_gate_4 (.A(and_b), .B(sel_and), .result(and_gate_4_result));
  AND_GATE and_gate_5 (.A(r_shift), .B(sel_Rshift), .result(and_gate_5_result));
  AND_GATE and_gate_6 (.A(l_shift), .B(sel_Lshift), .result(and_gate_6_result));
  or or_1 (mux_out, and_gate_1_result, and_gate_2_result, and_gate_3_result, and_gate_4_result, and_gate_5_result, and_gate_6_result);
endmodule

module hot_8_mux (
  input  sel_add,
  input  sel_sub,
  input  sel_xor,
  input  sel_and,
  input  sel_Rshift,
  input  sel_Lshift,
  input  [7:0] add,
  input  [7:0] l_shift,
  input  [7:0] and_b,
  input  [7:0] r_shift,
  input  [7:0] sub,
  input  [7:0] xor_in,
  output [7:0] resul
);

  ONE_hot_mux one_hot_mux_1 (
    .add(add[0]), .sub(sub[0]), .xor_b(xor_in[0]), .and_b(and_b[0]), .r_shift(r_shift[0]),
    .l_shift(l_shift[0]), .sel_add(sel_add), .sel_sub(sel_sub), .sel_xor(sel_xor), .sel_and(sel_and),
    .sel_Rshift(sel_Rshift), .sel_Lshift(sel_Lshift), .mux_out(resul[0]));
  ONE_hot_mux one_hot_mux_2 (
    .add(add[1]), .sub(sub[1]), .xor_b(xor_in[1]), .and_b(and_b[1]), .r_shift(r_shift[1]),
    .l_shift(l_shift[1]), .sel_add(sel_add), .sel_sub(sel_sub), .sel_xor(sel_xor), .sel_and(sel_and),
    .sel_Rshift(sel_Rshift), .sel_Lshift(sel_Lshift), .mux_out(resul[1]));
  ONE_hot_mux one_hot_mux_3 (
    .add(add[2]), .sub(sub[2]), .xor_b(xor_in[2]), .and_b(and_b[2]), .r_shift(r_shift[2]),
    .l_shift(l_shift[2]), .sel_add(sel_add), .sel_sub(sel_sub), .sel_xor(sel_xor), .sel_and(sel_and),
    .sel_Rshift(sel_Rshift), .sel_Lshift(sel_Lshift), .mux_out(resul[2]));
  ONE_hot_mux one_hot_mux_4 (
    .add(add[3]), .sub(sub[3]), .xor_b(xor_in[3]), .and_b(and_b[3]), .r_shift(r_shift[3]),
    .l_shift(l_shift[3]), .sel_add(sel_add), .sel_sub(sel_sub), .sel_xor(sel_xor), .sel_and(sel_and),
    .sel_Rshift(sel_Rshift), .sel_Lshift(sel_Lshift), .mux_out(resul[3]));
  ONE_hot_mux one_hot_mux_5 (
    .add(add[4]), .sub(sub[4]), .xor_b(xor_in[4]), .and_b(and_b[4]), .r_shift(r_shift[4]),
    .l_shift(l_shift[4]), .sel_add(sel_add), .sel_sub(sel_sub), .sel_xor(sel_xor), .sel_and(sel_and),
    .sel_Rshift(sel_Rshift), .sel_Lshift(sel_Lshift), .mux_out(resul[4]));
  ONE_hot_mux one_hot_mux_6 (
    .add(add[5]), .sub(sub[5]), .xor_b(xor_in[5]), .and_b(and_b[5]), .r_shift(r_shift[5]),
    .l_shift(l_shift[5]), .sel_add(sel_add), .sel_sub(sel_sub), .sel_xor(sel_xor), .sel_and(sel_and),
    .sel_Rshift(sel_Rshift), .sel_Lshift(sel_Lshift), .mux_out(resul[5]));
  ONE_hot_mux one_hot_mux_7 (
    .add(add[6]), .sub(sub[6]), .xor_b(xor_in[6]), .and_b(and_b[6]), .r_shift(r_shift[6]),
    .l_shift(l_shift[6]), .sel_add(sel_add), .sel_sub(sel_sub), .sel_xor(sel_xor), .sel_and(sel_and),
    .sel_Rshift(sel_Rshift), .sel_Lshift(sel_Lshift), .mux_out(resul[6]));
  ONE_hot_mux one_hot_mux_8 (
    .add(add[7]), .sub(sub[7]), .xor_b(xor_in[7]), .and_b(and_b[7]), .r_shift(r_shift[7]),
    .l_shift(l_shift[7]), .sel_add(sel_add), .sel_sub(sel_sub), .sel_xor(sel_xor), .sel_and(sel_and),
    .sel_Rshift(sel_Rshift), .sel_Lshift(sel_Lshift), .mux_out(resul[7]));
endmodule

module l_shift (
  input  [7:0] A,
  output [7:0] result
);


  assign result = {A[6:0], 1'b0};
endmodule

module R_shift (
  input  [7:0] A,
  output [7:0] result
);


  assign result = {1'b0, A[7:1]};
endmodule

module sub_8 (
  input  [7:0] A,
  input  [7:0] B,
  output [7:0] result
);

  wire [7:0] xor_8bit_1_result;

  XOR_8BIT xor_8bit_1 (.A(B), .B({8{1'b1}}), .result(xor_8bit_1_result));
  ADDER_8_BIT adder_8_bit_1 (.A(A), .carry(1'b1), .B(xor_8bit_1_result), .SUM(result));
endmodule

module MILESTONE (
  input  [7:0] A,
  input  [7:0] B,
  input  add,
  input  sub,
  input  xor_r,
  input  AND_R,
  input  r_shift_r,
  input  L_shift_r,
  output [7:0] result
);

  wire [7:0] adder_8_bit_1_sum, and_8bit_1_result, l_shift_1_result, r_shift_1_result, sub_8_1_result,
       xor_8bit_1_result;

  ADDER_8_BIT adder_8_bit_1 (.A(A), .B(B), .SUM(adder_8_bit_1_sum));  // open: carry
  sub_8 sub_8_1 (.A(A), .B(B), .result(sub_8_1_result));
  XOR_8BIT xor_8bit_1 (.A(A), .B(B), .result(xor_8bit_1_result));
  AND_8BIT and_8bit_1 (.A(A), .B(B), .result(and_8bit_1_result));
  R_shift r_shift_1 (.A(A), .result(r_shift_1_result));
  l_shift l_shift_1 (.A(A), .result(l_shift_1_result));
  hot_8_mux hot_8_mux_1 (
    .sel_add(add), .sel_sub(sub), .sel_xor(xor_r), .sel_and(AND_R), .sel_Rshift(r_shift_r),
    .sel_Lshift(L_shift_r), .add(adder_8_bit_1_sum), .l_shift(l_shift_1_result), .and_b(and_8bit_1_result),
    .r_shift(r_shift_1_result), .sub(sub_8_1_result), .xor_in(xor_8bit_1_result), .resul(result));
endmodule

module FINAL (
  input  [7:0] A,
  input  [7:0] B,
  input  ADD,
  input  SUB,
  input  XOR_r,
  input  AND_r,
  input  R_shift_r,
  input  L_shift_l,
  output [7:0] out_9
);

  // Probe on A
  // Probe on B
  MILESTONE milestone_1 (
    .A(A), .B(B), .add(ADD), .sub(SUB), .xor_r(XOR_r), .AND_R(AND_r), .r_shift_r(R_shift_r),
    .L_shift_r(L_shift_l), .result(out_9));
  // Probe on out_9
endmodule
